// Logisim project week3.circ as structural Verilog: 3 circuits, main circuit main
module main (
  input  in_1,
  input  in_2,
  input  in_3,
  input  in_4,
  input  in_5
);

  wire clock_1_out, d_ff_1_q, d_ff_2_q, d_ff_3_q, d_ff_4_q;

  Clock clock_1 (.out(clock_1_out));
  D_Flip_Flop d_ff_1 (.D(in_1), .clk(clock_1_out), .Q(d_ff_1_q));  // open: Qn, preset, reset
  LED led_1 (.in(d_ff_1_q));
  D_Flip_Flop d_ff_2 (.D(in_2), .clk(clock_1_out), .Q(d_ff_2_q));  // open: Qn, preset, reset
  LED led_2 (.in(d_ff_2_q));
  LED led_3 (.in(d_ff_2_q));
  D_Flip_Flop d_ff_3 (.D(in_3), .clk(clock_1_out), .Q(d_ff_3_q));  // open: Qn, preset, reset
  LED led_4 (.in(d_ff_3_q));
  LED led_5 (.in(d_ff_3_q));
  D_Flip_Flop d_ff_4 (.D(in_5), .clk(clock_1_out), .Q(d_ff_4_q));  // open: Qn, preset, reset
  LED led_6 (.in(d_ff_4_q));

  assign in_4 = in_3;
endmodule

module ripplecounter (
  input  in_1
);

  wire clock_1_out, j_k_ff_1_q, j_k_ff_1_qn, j_k_ff_3_q, j_k_ff_3_qn, j_k_ff_5_q, j_k_ff_5_qn, undriven,
       undriven_2, undriven_3, undriven_4, undriven_5, undriven_6, undriven_7, undriven_8, undriven_9,
       undriven_10, undriven_11, undriven_12, undriven_13, undriven_14, undriven_15;

  J_K_Flip_Flop #(.trigger("falling")) j_k_ff_1 (
    .J(undriven), .clk(undriven_2), .K(undriven_3), .Q(j_k_ff_1_q), .Qn(j_k_ff_1_qn), .preset(undriven_4),
    .reset(in_1));
  J_K_Flip_Flop #(.trigger("falling")) j_k_ff_2 (
    .J(undriven), .clk(undriven_2), .K(undriven_3), .Q(j_k_ff_1_q), .Qn(j_k_ff_1_qn), .preset(undriven_4),
    .reset(in_1));
  J_K_Flip_Flop #(.trigger("falling")) j_k_ff_3 (
    .J(undriven_6), .clk(undriven_7), .K(undriven_8), .Q(j_k_ff_3_q), .Qn(j_k_ff_3_qn), .preset(undriven_9),
    .reset(in_1));
  J_K_Flip_Flop #(.trigger("falling")) j_k_ff_4 (
    .J(undriven_6), .clk(undriven_7), .K(undriven_8), .Q(j_k_ff_3_q), .Qn(j_k_ff_3_qn), .preset(undriven_9),
    .reset(in_1));
  LED led_1 (.in(undriven_5));
  LED led_2 (.in(undriven_11));
  J_K_Flip_Flop #(.trigger("falling")) j_k_ff_5 (
    .J(undriven_12), .clk(undriven_13), .K(undriven_14), .Q(j_k_ff_5_q), .Qn(j_k_ff_5_qn),
    .preset(undriven_15), .reset(in_1));
  J_K_Flip_Flop #(.trigger("falling")) j_k_ff_6 (
    .J(undriven_12), .clk(undriven_13), .K(undriven_14), .Q(j_k_ff_5_q), .Qn(j_k_ff_5_qn),
    .preset(undriven_15), .reset(in_1));
  Clock clock_1 (.out(clock_1_out));
  LED led_3 (.in(undriven_10));
endmodule

module countingto6 (
  input  in_1,
  input  in_2
);

  wire and_1_out, clock_1_out, j_k_ff_1_q, j_k_ff_1_qn, j_k_ff_3_q, j_k_ff_3_qn, j_k_ff_5_q, j_k_ff_5_qn,
       undriven, undriven_2, undriven_3, undriven_4, undriven_5, undriven_6, undriven_7, undriven_8,
       undriven_9, undriven_10, undriven_11, undriven_12;
  wire [2:0] undriven_13;

  Clock clock_1 (.out(clock_1_out));
  J_K_Flip_Flop #(.trigger("falling")) j_k_ff_1 (
    .J(undriven), .clk(undriven_2), .K(undriven_3), .Q(j_k_ff_1_q), .Qn(j_k_ff_1_qn), .preset(undriven_4),
    .reset(in_1));
  J_K_Flip_Flop #(.trigger("falling")) j_k_ff_2 (
    .J(undriven), .clk(undriven_2), .K(undriven_3), .Q(j_k_ff_1_q), .Qn(j_k_ff_1_qn), .preset(undriven_4),
    .reset(in_1));
  J_K_Flip_Flop #(.trigger("falling")) j_k_ff_3 (
    .J(undriven_5), .clk(undriven_6), .K(undriven_7), .Q(j_k_ff_3_q), .Qn(j_k_ff_3_qn), .preset(undriven_8),
    .reset(in_1));
  J_K_Flip_Flop #(.trigger("falling")) j_k_ff_4 (
    .J(undriven_5), .clk(undriven_6), .K(undriven_7), .Q(j_k_ff_3_q), .Qn(j_k_ff_3_qn), .preset(undriven_8),
    .reset(in_1));
  LED led_1 (.in(undriven_13[0]));
  LED led_2 (.in(undriven_13[1]));
  J_K_Flip_Flop #(.trigger("falling")) j_k_ff_5 (
    .J(undriven_9), .clk(undriven_10), .K(undriven_11), .Q(j_k_ff_5_q), .Qn(j_k_ff_5_qn),
    .preset(undriven_12), .reset(in_1));
  J_K_Flip_Flop #(.trigger("falling")) j_k_ff_6 (
    .J(undriven_9), .clk(undriven_10), .K(undriven_11), .Q(j_k_ff_5_q), .Qn(j_k_ff_5_qn),
    .preset(undriven_12), .reset(in_1));
  LED led_3 (.in(undriven_13[2]));
  and and_1 (and_1_out, undriven_13[1], undriven_13[2]);
  Hex_Digit_Display hex_digit_display_1 (.value({in_2, undriven_13}));  // open: dp
endmodule
