// Logisim project assign1.circ as structural Verilog: 5 circuits, main circuit main
module main (
  input  VolUp,
  input  VolDown
);

  wire and_1_out, and_2_out, and_3_out, and_4_out, and_5_out, and_6_out, and_7_out, and_8_out, and_9_out,
       and_10_out, and_11_out, and_12_out, and_13_out, and_14_out, and_15_out, and_16_out, and_17_out,
       clock_1_out, d_ff_1_q, d_ff_2_q, d_ff_3_q, d_ff_4_q, d_ff_5_q, d_ff_6_q, d_ff_7_q, d_ff_8_q, d_ff_9_q,
       d_ff_10_q, j_k_ff_1_q, j_k_ff_1_qn, not_1_out, or_1_out, or_2_out, or_3_out, or_4_out, or_5_out,
       or_6_out, or_7_out, or_8_out, or_9_out, or_10_out, Pause_out, Play_out;

  Clock clock_1 (.out(clock_1_out));
  Button Play (.out(Play_out));
  Button Pause (.out(Pause_out));
  or or_1 (or_1_out, VolDown, VolUp);
  D_Flip_Flop d_ff_1 (.D(Play_out), .clk(clock_1_out), .Q(d_ff_1_q), .preset(Play_out));  // open: Qn, reset
  D_Flip_Flop d_ff_2 (.D(Pause_out), .clk(clock_1_out), .Q(d_ff_2_q), .preset(Pause_out));  // open: Qn, reset
  not not_1 (not_1_out, VolUp);
  and and_1 (and_1_out, VolUp, VolUp);
  and and_2 (and_2_out, not_1_out, d_ff_4_q);
  or or_2 (or_2_out, and_1_out, and_2_out);
  D_Flip_Flop d_ff_3 (.D(or_2_out), .clk(and_3_out), .Q(d_ff_3_q));  // open: Qn, preset, reset
  and and_3 (and_3_out, or_1_out, clock_1_out);
  or or_3 (or_3_out, d_ff_1_q, d_ff_2_q);
  and and_4 (and_4_out, d_ff_3_q, VolUp);
  or or_4 (or_4_out, and_4_out, and_5_out);
  LED Vol0 (.in(d_ff_3_q));
  J_K_Flip_Flop j_k_ff_1 (
    .J(or_3_out), .K(d_ff_2_q), .clk(clock_1_out), .Q(j_k_ff_1_q), .Qn(j_k_ff_1_qn));  // open: preset, reset
  and and_5 (and_5_out, not_1_out, d_ff_5_q);
  D_Flip_Flop d_ff_4 (.D(or_4_out), .clk(and_3_out), .Q(d_ff_4_q));  // open: Qn, preset, reset
  LED Vol1 (.in(d_ff_4_q));
  LED Playing (.in(j_k_ff_1_q));
  LED Paused (.in(j_k_ff_1_qn));
  and and_6 (and_6_out, d_ff_4_q, VolUp);
  and and_7 (and_7_out, not_1_out, d_ff_6_q);
  or or_5 (or_5_out, and_6_out, and_7_out);
  D_Flip_Flop d_ff_5 (.D(or_5_out), .clk(and_3_out), .Q(d_ff_5_q));  // open: Qn, preset, reset
  and and_8 (and_8_out, d_ff_5_q, VolUp);
  and and_9 (and_9_out, not_1_out, d_ff_7_q);
  or or_6 (or_6_out, and_8_out, and_9_out);
  D_Flip_Flop d_ff_6 (.D(or_6_out), .clk(and_3_out), .Q(d_ff_6_q));  // open: Qn, preset, reset
  LED Vol2 (.in(d_ff_5_q));
  and and_10 (and_10_out, d_ff_6_q, VolUp);
  LED Vol3 (.in(d_ff_6_q));
  and and_11 (and_11_out, not_1_out, d_ff_8_q);
  or or_7 (or_7_out, and_10_out, and_11_out);
  D_Flip_Flop d_ff_7 (.D(or_7_out), .clk(and_3_out), .Q(d_ff_7_q));  // open: Qn, preset, reset
  LED Vol4 (.in(d_ff_7_q));
  and and_12 (and_12_out, d_ff_7_q, VolUp);
  and and_13 (and_13_out, not_1_out, d_ff_9_q);
  or or_8 (or_8_out, and_12_out, and_13_out);
  D_Flip_Flop d_ff_8 (.D(or_8_out), .clk(and_3_out), .Q(d_ff_8_q));  // open: Qn, preset, reset
  and and_14 (and_14_out, d_ff_8_q, VolUp);
  or or_9 (or_9_out, and_14_out, and_16_out);
  D_Flip_Flop d_ff_9 (.D(or_9_out), .clk(and_3_out), .Q(d_ff_9_q));  // open: Qn, preset, reset
  LED Vol5 (.in(d_ff_8_q));
  and and_15 (and_15_out, d_ff_9_q, VolUp);
  and and_16 (and_16_out, not_1_out, d_ff_10_q);
  LED Vol6 (.in(d_ff_9_q));
  and and_17 (and_17_out, not_1_out, 1'b0);
  or or_10 (or_10_out, and_15_out, and_17_out);
  D_Flip_Flop d_ff_10 (.D(or_10_out), .clk(and_3_out), .Q(d_ff_10_q));  // open: Qn, preset, reset
  LED Vol7 (.in(d_ff_10_q));
endmodule

module StageOne (
);

  wire clock_1_out, d_ff_1_q, d_ff_2_q, j_k_ff_1_q, j_k_ff_1_qn, or_1_out, Pause_out, Play_out;

  Clock clock_1 (.out(clock_1_out));
  Button Play (.out(Play_out));
  Button Pause (.out(Pause_out));
  D_Flip_Flop d_ff_1 (.D(Play_out), .clk(clock_1_out), .Q(d_ff_1_q), .preset(Play_out));  // open: Qn, reset
  D_Flip_Flop d_ff_2 (.D(Pause_out), .clk(clock_1_out), .Q(d_ff_2_q), .preset(Pause_out));  // open: Qn, reset
  or or_1 (or_1_out, d_ff_1_q, d_ff_2_q);
  J_K_Flip_Flop j_k_ff_1 (
    .J(or_1_out), .K(d_ff_2_q), .clk(clock_1_out), .Q(j_k_ff_1_q), .Qn(j_k_ff_1_qn));  // open: preset, reset
  LED Playing (.in(j_k_ff_1_q));
  LED Paused (.in(j_k_ff_1_qn));
endmodule

module StageTwo (
  input  VolUp,
  input  VolDown
);

  wire and_1_out, and_2_out, and_3_out, and_4_out, and_5_out, and_6_out, and_7_out, and_8_out, and_9_out,
       and_10_out, and_11_out, and_12_out, and_13_out, and_14_out, and_15_out, and_16_out, and_17_out,
       clock_1_out, d_ff_1_q, d_ff_2_q, d_ff_3_q, d_ff_4_q, d_ff_5_q, d_ff_6_q, d_ff_7_q, d_ff_8_q,
       not_1_out, or_1_out, or_2_out, or_3_out, or_4_out, or_5_out, or_6_out, or_7_out, or_8_out, or_9_out;

  or or_1 (or_1_out, VolDown, VolUp);
  Clock clock_1 (.out(clock_1_out));
  not not_1 (not_1_out, VolUp);
  and and_1 (and_1_out, not_1_out, d_ff_2_q);
  and and_2 (and_2_out, VolUp, VolUp);
  or or_2 (or_2_out, and_2_out, and_1_out);
  D_Flip_Flop d_ff_1 (.D(or_2_out), .clk(and_3_out), .Q(d_ff_1_q));  // open: Qn, preset, reset
  and and_3 (and_3_out, or_1_out, clock_1_out);
  and and_4 (and_4_out, d_ff_1_q, VolUp);
  or or_3 (or_3_out, and_4_out, and_5_out);
  LED Vol0 (.in(d_ff_1_q));
  and and_5 (and_5_out, not_1_out, d_ff_3_q);
  D_Flip_Flop d_ff_2 (.D(or_3_out), .clk(and_3_out), .Q(d_ff_2_q));  // open: Qn, preset, reset
  LED Vol1 (.in(d_ff_2_q));
  and and_6 (and_6_out, d_ff_2_q, VolUp);
  and and_7 (and_7_out, not_1_out, d_ff_4_q);
  or or_4 (or_4_out, and_6_out, and_7_out);
  D_Flip_Flop d_ff_3 (.D(or_4_out), .clk(and_3_out), .Q(d_ff_3_q));  // open: Qn, preset, reset
  and and_8 (and_8_out, d_ff_3_q, VolUp);
  and and_9 (and_9_out, not_1_out, d_ff_5_q);
  or or_5 (or_5_out, and_8_out, and_9_out);
  D_Flip_Flop d_ff_4 (.D(or_5_out), .clk(and_3_out), .Q(d_ff_4_q));  // open: Qn, preset, reset
  LED Vol2 (.in(d_ff_3_q));
  and and_10 (and_10_out, d_ff_4_q, VolUp);
  LED Vol3 (.in(d_ff_4_q));
  and and_11 (and_11_out, not_1_out, d_ff_6_q);
  or or_6 (or_6_out, and_10_out, and_11_out);
  D_Flip_Flop d_ff_5 (.D(or_6_out), .clk(and_3_out), .Q(d_ff_5_q));  // open: Qn, preset, reset
  LED Vol4 (.in(d_ff_5_q));
  and and_12 (and_12_out, not_1_out, d_ff_7_q);
  and and_13 (and_13_out, d_ff_5_q, VolUp);
  or or_7 (or_7_out, and_13_out, and_12_out);
  D_Flip_Flop d_ff_6 (.D(or_7_out), .clk(and_3_out), .Q(d_ff_6_q));  // open: Qn, preset, reset
  and and_14 (and_14_out, d_ff_6_q, VolUp);
  or or_8 (or_8_out, and_14_out, and_15_out);
  D_Flip_Flop d_ff_7 (.D(or_8_out), .clk(and_3_out), .Q(d_ff_7_q));  // open: Qn, preset, reset
  LED Vol5 (.in(d_ff_6_q));
  and and_15 (and_15_out, not_1_out, d_ff_8_q);
  and and_16 (and_16_out, d_ff_7_q, VolUp);
  LED Vol6 (.in(d_ff_7_q));
  and and_17 (and_17_out, not_1_out, 1'b0);
  or or_9 (or_9_out, and_16_out, and_17_out);
  D_Flip_Flop d_ff_8 (.D(or_9_out), .clk(and_3_out), .Q(d_ff_8_q));  // open: Qn, preset, reset
  LED Vol7 (.in(d_ff_8_q));
endmodule

module StageThree (
);

  wire and_1_out, and_2_out, and_3_out, and_4_out, and_5_out, and_6_out, and_7_out, and_8_out, and_9_out,
       and_10_out, and_11_out, and_12_out, and_13_out, and_14_out, and_15_out, and_16_out, clock_1_out,
       NextTrack_out, or_1_out, or_2_out, or_3_out, or_4_out, or_5_out, or_6_out, or_7_out, or_8_out,
       or_9_out, or_10_out, or_11_out, or_12_out, or_13_out, PreviousTrack_out, t_ff_1_q, t_ff_1_qn,
       t_ff_2_q, t_ff_2_qn, t_ff_3_q, t_ff_3_qn, t_ff_4_q, t_ff_4_qn, t_ff_5_q, t_ff_5_qn, t_ff_6_q,
       t_ff_6_qn, t_ff_7_q, t_ff_8_q;
  wire [3:0] d_ff_1_q, d_ff_2_q;

  Clock clock_1 (.out(clock_1_out));
  Button NextTrack (.out(NextTrack_out));
  Button PreviousTrack (.out(PreviousTrack_out));
  or or_1 (or_1_out, and_9_out, and_15_out);
  T_Flip_Flop t_ff_1 (
    .T(or_2_out), .clk(clock_1_out), .Q(t_ff_1_q), .Qn(t_ff_1_qn), .reset(and_15_out));  // open: preset
  or or_2 (or_2_out, NextTrack_out, PreviousTrack_out);
  T_Flip_Flop t_ff_2 (.T(or_3_out), .clk(or_1_out), .Q(t_ff_2_q), .Qn(t_ff_2_qn), .reset(and_16_out));  // open: preset
  or or_3 (or_3_out, NextTrack_out, PreviousTrack_out);
  and and_1 (and_1_out, NextTrack_out, t_ff_1_q);
  and and_2 (and_2_out, t_ff_1_qn, PreviousTrack_out);
  and and_3 (and_3_out, NextTrack_out, t_ff_2_q);
  and and_4 (and_4_out, t_ff_2_qn, PreviousTrack_out);
  T_Flip_Flop t_ff_3 (.T(or_4_out), .clk(clock_1_out), .Q(t_ff_3_q), .Qn(t_ff_3_qn), .reset(or_5_out));  // open: preset
  or or_4 (or_4_out, and_1_out, and_2_out);
  or or_5 (or_5_out, and_15_out, and_9_out);
  T_Flip_Flop t_ff_4 (.T(or_6_out), .clk(or_1_out), .Q(t_ff_4_q), .Qn(t_ff_4_qn), .reset(or_7_out));  // open: preset
  or or_6 (or_6_out, and_3_out, and_4_out);
  or or_7 (or_7_out, and_16_out, and_12_out);
  and and_5 (and_5_out, and_1_out, t_ff_3_q);
  and and_6 (and_6_out, t_ff_3_qn, and_2_out);
  and and_7 (and_7_out, and_3_out, t_ff_4_q);
  and and_8 (and_8_out, t_ff_4_qn, and_4_out);
  T_Flip_Flop t_ff_5 (
    .T(or_8_out), .clk(clock_1_out), .Q(t_ff_5_q), .Qn(t_ff_5_qn), .reset(or_10_out));  // open: preset
  or or_8 (or_8_out, and_5_out, and_6_out);
  T_Flip_Flop t_ff_6 (.T(or_9_out), .clk(or_1_out), .Q(t_ff_6_q), .Qn(t_ff_6_qn), .reset(or_11_out));  // open: preset
  or or_9 (or_9_out, and_7_out, and_8_out);
  or or_10 (or_10_out, and_15_out, and_9_out);
  or or_11 (or_11_out, and_16_out, and_12_out);
  and and_9 (and_9_out, PreviousTrack_out, t_ff_1_q, t_ff_3_q, t_ff_5_q, t_ff_7_q);
  and and_10 (and_10_out, and_5_out, t_ff_5_q);
  or or_12 (or_12_out, and_10_out, and_11_out);
  and and_11 (and_11_out, t_ff_5_qn, and_6_out);
  and and_12 (and_12_out, PreviousTrack_out, t_ff_2_q, t_ff_4_q, t_ff_6_q, t_ff_8_q);
  and and_13 (and_13_out, and_7_out, t_ff_6_q);
  or or_13 (or_13_out, and_13_out, and_14_out);
  and and_14 (and_14_out, t_ff_6_qn, and_8_out);
  and and_15 (and_15_out, NextTrack_out, t_ff_3_q, t_ff_7_q);
  T_Flip_Flop t_ff_7 (.T(or_12_out), .clk(clock_1_out), .Q(t_ff_7_q), .reset(and_15_out));  // open: Qn, preset
  and and_16 (and_16_out, NextTrack_out, t_ff_4_q, t_ff_8_q);
  T_Flip_Flop t_ff_8 (.T(or_13_out), .clk(or_1_out), .Q(t_ff_8_q), .reset(and_16_out));  // open: Qn, preset
  D_Flip_Flop d_ff_1 (.D(t_ff_1_q), .clk(clock_1_out), .Q(d_ff_1_q[0]));  // open: Qn, preset, reset
  D_Flip_Flop d_ff_2 (.D(t_ff_2_q), .clk(clock_1_out), .Q(d_ff_2_q[0]));  // open: Qn, preset, reset
  D_Flip_Flop d_ff_3 (.D(t_ff_3_q), .clk(clock_1_out), .Q(d_ff_1_q[1]));  // open: Qn, preset, reset
  D_Flip_Flop d_ff_4 (.D(t_ff_4_q), .clk(clock_1_out), .Q(d_ff_2_q[1]));  // open: Qn, preset, reset
  D_Flip_Flop d_ff_5 (.D(t_ff_5_q), .clk(clock_1_out), .Q(d_ff_1_q[2]));  // open: Qn, preset, reset
  D_Flip_Flop d_ff_6 (.D(t_ff_6_q), .clk(clock_1_out), .Q(d_ff_2_q[2]));  // open: Qn, preset, reset
  D_Flip_Flop d_ff_7 (.D(t_ff_7_q), .clk(clock_1_out), .Q(d_ff_1_q[3]));  // open: Qn, preset, reset
  D_Flip_Flop d_ff_8 (.D(t_ff_8_q), .clk(clock_1_out), .Q(d_ff_2_q[3]));  // open: Qn, preset, reset
  Hex_Digit_Display hex_digit_display_1 (.value(d_ff_2_q));  // open: dp
  Hex_Digit_Display hex_digit_display_2 (.value(d_ff_1_q));  // open: dp
endmodule

module ButtonStateHolder (
);

  wire button_1_out, clock_1_out, d_ff_1_q;

  Button button_1 (.out(button_1_out));
  Clock clock_1 (.out(clock_1_out));
  D_Flip_Flop d_ff_1 (.D(button_1_out), .clk(clock_1_out), .Q(d_ff_1_q), .preset(button_1_out));  // open: Qn, reset
  D_Flip_Flop d_ff_2 (.D(d_ff_1_q), .clk(clock_1_out));  // open: Q, Qn, preset, reset
endmodule
